// Logisim project ProgettoInLogisim.circ as structural Verilog: 1 circuit, main circuit main
module main (
  input  x0,
  input  y0,
  input  x1,
  input  y1
);

  wire nand_1_out, nand_2_out, nand_3_out, nand_4_out, nand_5_out, nand_6_out, nand_7_out, nand_8_out,
       nand_9_out, nand_10_out, nand_11_out, nand_12_out, nand_13_out, nand_14_out, nand_15_out, nand_16_out,
       nand_17_out, nand_18_out, nand_19_out, not_1_out;

  nand nand_1 (nand_1_out, x1, nand_3_out);
  nand nand_2 (nand_2_out, x0, y0);
  nand nand_3 (nand_3_out, nand_2_out, nand_2_out);
  nand nand_4 (nand_4_out, x1, y1);
  nand nand_5 (nand_5_out, nand_1_out, nand_4_out);
  not not_1 (not_1_out, nand_5_out);
  nand nand_6 (nand_6_out, not_1_out, nand_8_out);
  nand nand_7 (nand_7_out, x0, nand_10_out);
  nand nand_8 (nand_8_out, y1, nand_3_out);
  nand nand_9 (nand_9_out, nand_3_out, nand_17_out);
  nand nand_10 (nand_10_out, x0, y0);
  nand nand_11 (nand_11_out, nand_10_out, y0);
  nand nand_12 (nand_12_out, nand_7_out, nand_11_out);
  nand nand_13 (nand_13_out, x1, y1);
  nand nand_14 (nand_14_out, x1, nand_13_out);
  nand nand_15 (nand_15_out, nand_13_out, y1);
  nand nand_16 (nand_16_out, nand_14_out, nand_15_out);
  nand nand_17 (nand_17_out, nand_3_out, nand_16_out);
  nand nand_18 (nand_18_out, nand_17_out, nand_16_out);
  nand nand_19 (nand_19_out, nand_9_out, nand_18_out);
  LED bit0 (.in(nand_12_out));
  LED bit1 (.in(nand_19_out));
  LED bit2 (.in(nand_6_out));

  // Notes on the sheet:
  //   primo addendo
  //   half adder
  //   full adder
  //   secondo addendo
  //   output
endmodule
